// Logisim project MON PROJET.circ as structural Verilog: 16 circuits, main circuit UNITE-LOGIQUE
// ET-LOG
module ET_LOGIQUE (
  input  in_1,
  input  in_2,
  input  in_3,
  input  in_4,
  input  in_5,
  input  in_6,
  input  in_7,
  input  in_8,
  output out_9,
  output out_10,
  output out_11,
  output out_12
);

  and and_1 (out_12, in_4, in_8);
  and and_2 (out_11, in_3, in_7);
  and and_3 (out_10, in_2, in_6);
  and and_4 (out_9, in_1, in_5);
endmodule

// COMP
module COMPARATEUR (
  input  in_1,
  input  in_2,
  input  in_3,
  input  in_4,
  input  in_5,
  input  in_6,
  input  in_7,
  input  in_8,
  output out_9,
  output out_10,
  output out_11,
  output out_12
);

  xnor xnor_1 (out_12, in_4, in_8);
  xnor xnor_2 (out_11, in_3, in_7);
  xnor xnor_3 (out_10, in_2, in_6);
  xnor xnor_4 (out_9, in_1, in_5);
endmodule

// DMUX
module DEMULTIPLEXEUR (
  input  in_1,
  input  in_2,
  output out_3,
  output out_4
);

  Demultiplexer demultiplexer_1 (.out0(out_3), .out1(out_4), .in(in_1), .sel(in_2));  // open: en
endmodule

// MUX
module MULTIPLEXEUR (
  input  in_1,
  input  in_2,
  input  in_3,
  output out_4
);

  Multiplexer multiplexer_1 (.in0(in_1), .in1(in_2), .out(out_4), .sel(in_3));  // open: en
endmodule

// TRANS
module TRANSCODEUR (
  input  A,
  input  B,
  input  C,
  input  D,
  output a_2,
  output b_2,
  output c_2,
  output d_2,
  output e,
  output f,
  output g
);

  wire and_1_out, and_2_out, and_3_out, and_4_out, and_5_out, and_6_out, and_7_out, and_8_out, and_9_out,
       and_10_out, and_11_out, and_12_out, and_13_out, and_14_out, and_15_out, not_1_out, not_2_out,
       not_3_out, not_4_out, not_5_out, not_6_out, not_7_out, not_8_out, not_9_out, not_10_out, not_11_out,
       not_12_out, not_13_out, not_14_out, not_15_out, not_16_out, not_17_out, not_18_out, not_19_out,
       not_20_out, not_21_out;

  not not_1 (not_1_out, B);
  and and_1 (and_1_out, not_1_out, not_2_out);
  not not_2 (not_2_out, D);
  and and_2 (and_2_out, B, D);
  not not_3 (not_3_out, B);
  not not_4 (not_4_out, C);
  and and_3 (and_3_out, not_4_out, not_5_out);
  not not_5 (not_5_out, D);
  and and_4 (and_4_out, C, D);
  not not_6 (not_6_out, C);
  or or_1 (c_2, not_6_out, D, B);
  not not_7 (not_7_out, B);
  and and_5 (and_5_out, not_7_out, not_8_out);
  not not_8 (not_8_out, D);
  not not_9 (not_9_out, B);
  and and_6 (and_6_out, not_9_out, C);
  and and_7 (and_7_out, C, not_10_out);
  not not_10 (not_10_out, D);
  not not_11 (not_11_out, C);
  and and_8 (and_8_out, B, not_11_out, D);
  not not_12 (not_12_out, B);
  and and_9 (and_9_out, not_12_out, not_13_out);
  not not_13 (not_13_out, D);
  and and_10 (and_10_out, C, not_14_out);
  not not_14 (not_14_out, D);
  not not_15 (not_15_out, C);
  and and_11 (and_11_out, not_15_out, not_16_out);
  not not_16 (not_16_out, D);
  and and_12 (and_12_out, B, not_17_out);
  not not_17 (not_17_out, C);
  and and_13 (and_13_out, B, not_18_out);
  not not_18 (not_18_out, D);
  not not_19 (not_19_out, D);
  not not_20 (not_20_out, B);
  and and_14 (and_14_out, not_20_out, C);
  and and_15 (and_15_out, B, not_21_out);
  not not_21 (not_21_out, C);
  or or_2 (a_2, and_1_out, C, and_2_out);
  or or_3 (b_2, not_3_out, and_3_out, and_4_out);
  or or_4 (d_2, and_5_out, and_6_out, and_7_out, and_8_out);
  or or_5 (e, and_9_out, and_10_out);
  or or_6 (f, and_11_out, and_12_out, and_13_out);
  or or_7 (g, not_19_out, and_14_out, and_15_out);
endmodule

// A+
module HALF_ADD (
  input  in_1,
  input  in_2,
  input  in_3,
  output out_4,
  output out_5
);

  wire and_1_out, and_2_out, xor_1_out;

  xor xor_1 (xor_1_out, in_2, in_3);
  and and_1 (and_1_out, in_2, in_3);
  xor xor_2 (out_5, in_1, xor_1_out);
  and and_2 (and_2_out, xor_1_out, in_1);
  or or_1 (out_4, and_2_out, and_1_out);
endmodule

// ADD-COOMPL
module FULL_ADD (
  input  in_1,
  input  in_2,
  input  in_3,
  input  in_4,
  input  in_5,
  input  in_6,
  input  in_7,
  input  in_8,
  input  in_9,
  output out_10,
  output out_11,
  output out_12,
  output out_13
);

  wire half_add_1_out_4, half_add_2_out_4, half_add_3_out_4;

  HALF_ADD half_add_1 (.in_1(in_9), .in_2(in_8), .in_3(in_4), .out_4(half_add_1_out_4), .out_5(out_13));
  HALF_ADD half_add_2 (.in_1(half_add_1_out_4), .in_2(in_7), .in_3(in_3), .out_4(half_add_2_out_4), .out_5(out_12));
  HALF_ADD half_add_3 (.in_1(half_add_2_out_4), .in_2(in_6), .in_3(in_2), .out_4(half_add_3_out_4));  // open: out_5
  HALF_ADD half_add_4 (.in_1(half_add_3_out_4), .in_2(in_5), .in_3(in_1), .out_4(out_10), .out_5(out_11));
endmodule

// ALU
module _1BIT_UAL (
  input  in_1,
  input  in_2,
  input  in_3,
  input  [1:0] in_4,
  input  in_5,
  output out_6,
  output out_7
);

  wire adder_1_out, and_1_out, multiplexer_1_out, not_1_out, or_1_out;

  not not_1 (not_1_out, in_1);
  Multiplexer multiplexer_1 (.in0(not_1_out), .in1(in_1), .out(multiplexer_1_out), .sel(in_5));  // open: en
  and and_1 (and_1_out, in_2, multiplexer_1_out);
  or or_1 (or_1_out, in_2, multiplexer_1_out);
  Adder #(.width(1)) adder_1 (.a(in_2), .b(multiplexer_1_out), .out(adder_1_out), .cin(in_3), .cout(out_7));
  Multiplexer #(.select(2)) multiplexer_2 (
    .in0(and_1_out), .in1(or_1_out), .in2(adder_1_out), .out(out_6), .sel(in_4));  // open: in3, en
endmodule

// UAL 16 BIT
module UAL (
  input  Carryin,
  input  [15:0] A,
  input  [15:0] B,
  input  Binvert,
  input  [1:0] Operation,
  input  [15:0] result,
  input  zero,
  input  Overflow,
  output Carryout
);

  wire n1bit_ual_1_out_7, n1bit_ual_2_out_7, n1bit_ual_3_out_7, n1bit_ual_4_out_7, n1bit_ual_5_out_7,
       n1bit_ual_6_out_7, n1bit_ual_7_out_7, n1bit_ual_8_out_7, n1bit_ual_9_out_7, n1bit_ual_10_out_7,
       n1bit_ual_11_out_7, n1bit_ual_12_out_7, n1bit_ual_13_out_7, n1bit_ual_14_out_7, n1bit_ual_15_out_7,
       nor_1_out;

  _1BIT_UAL u_1bit_ual_1 (
    .out_6(result[0]), .in_1(B[0]), .in_2(A[0]), .in_3(Carryin), .in_5(Binvert), .out_7(n1bit_ual_1_out_7),
    .in_4(Operation));
  _1BIT_UAL u_1bit_ual_2 (
    .out_6(result[1]), .in_1(B[1]), .in_2(A[1]), .in_3(n1bit_ual_1_out_7), .in_5(Binvert),
    .out_7(n1bit_ual_2_out_7), .in_4(Operation));
  _1BIT_UAL u_1bit_ual_3 (
    .out_6(result[2]), .in_1(B[2]), .in_2(A[2]), .in_3(n1bit_ual_2_out_7), .in_5(Binvert),
    .out_7(n1bit_ual_3_out_7), .in_4(Operation));
  _1BIT_UAL u_1bit_ual_4 (
    .out_6(result[3]), .in_1(B[3]), .in_2(A[3]), .in_3(n1bit_ual_3_out_7), .in_5(Binvert),
    .out_7(n1bit_ual_4_out_7), .in_4(Operation));
  _1BIT_UAL u_1bit_ual_5 (
    .out_6(result[4]), .in_1(B[4]), .in_2(A[4]), .in_3(n1bit_ual_4_out_7), .in_5(Binvert),
    .out_7(n1bit_ual_5_out_7), .in_4(Operation));
  _1BIT_UAL u_1bit_ual_6 (
    .out_6(result[5]), .in_1(B[5]), .in_2(A[5]), .in_3(n1bit_ual_5_out_7), .in_5(Binvert),
    .out_7(n1bit_ual_6_out_7), .in_4(Operation));
  _1BIT_UAL u_1bit_ual_7 (
    .out_6(result[6]), .in_1(B[6]), .in_2(A[6]), .in_3(n1bit_ual_6_out_7), .in_5(Binvert),
    .out_7(n1bit_ual_7_out_7), .in_4(Operation));
  _1BIT_UAL u_1bit_ual_8 (
    .out_6(result[7]), .in_1(B[7]), .in_2(A[7]), .in_3(n1bit_ual_7_out_7), .in_5(Binvert),
    .out_7(n1bit_ual_8_out_7), .in_4(Operation));
  _1BIT_UAL u_1bit_ual_9 (
    .out_6(result[8]), .in_1(B[8]), .in_2(A[8]), .in_3(n1bit_ual_8_out_7), .in_5(Binvert),
    .out_7(n1bit_ual_9_out_7), .in_4(Operation));
  _1BIT_UAL u_1bit_ual_10 (
    .out_6(result[9]), .in_1(B[9]), .in_2(A[9]), .in_3(n1bit_ual_9_out_7), .in_5(Binvert),
    .out_7(n1bit_ual_10_out_7), .in_4(Operation));
  _1BIT_UAL u_1bit_ual_11 (
    .out_6(result[10]), .in_1(B[10]), .in_2(A[10]), .in_3(n1bit_ual_10_out_7), .in_5(Binvert),
    .out_7(n1bit_ual_11_out_7), .in_4(Operation));
  _1BIT_UAL u_1bit_ual_12 (
    .out_6(result[11]), .in_1(B[11]), .in_2(A[11]), .in_3(n1bit_ual_11_out_7), .in_5(Binvert),
    .out_7(n1bit_ual_12_out_7), .in_4(Operation));
  _1BIT_UAL u_1bit_ual_13 (
    .out_6(result[12]), .in_1(B[12]), .in_2(A[12]), .in_3(n1bit_ual_12_out_7), .in_5(Binvert),
    .out_7(n1bit_ual_13_out_7), .in_4(Operation));
  _1BIT_UAL u_1bit_ual_14 (
    .out_6(result[13]), .in_1(B[13]), .in_2(A[13]), .in_3(n1bit_ual_13_out_7), .in_5(Binvert),
    .out_7(n1bit_ual_14_out_7), .in_4(Operation));
  _1BIT_UAL u_1bit_ual_15 (
    .out_6(result[14]), .in_1(B[14]), .in_2(A[14]), .in_3(n1bit_ual_14_out_7), .in_5(Binvert),
    .out_7(n1bit_ual_15_out_7), .in_4(Operation));
  _1BIT_UAL u_1bit_ual_16 (
    .out_6(result[15]), .in_1(B[15]), .in_2(A[15]), .in_3(n1bit_ual_15_out_7), .in_5(Binvert),
    .out_7(Carryout), .in_4(Operation));
  nor nor_1 (nor_1_out, result[0], result[1], result[2], result[3], result[4], result[5], result[6], result[7], result[8], result[9], result[10], result[11], result[12], result[13], result[14], result[15]);
  xor xor_1 (Overflow, n1bit_ual_15_out_7, Carryout);
endmodule

// UL
module UNITE_LOGIQUE (
  input  Selectop,
  input  B3,
  input  B2,
  input  B1,
  input  B0,
  input  A0,
  input  A1,
  input  A2,
  input  A3,
  output R0,
  output R1,
  output R2,
  output R3
);

  wire comparateur_1_out_9, comparateur_1_out_10, comparateur_1_out_11, comparateur_1_out_12,
       demultiplexeur_1_out_3, demultiplexeur_1_out_4, demultiplexeur_2_out_3, demultiplexeur_2_out_4,
       demultiplexeur_3_out_3, demultiplexeur_3_out_4, demultiplexeur_4_out_3, demultiplexeur_4_out_4,
       demultiplexeur_5_out_3, demultiplexeur_5_out_4, demultiplexeur_6_out_3, demultiplexeur_6_out_4,
       demultiplexeur_7_out_3, demultiplexeur_7_out_4, demultiplexeur_8_out_3, demultiplexeur_8_out_4,
       et_logique_1_out_9, et_logique_1_out_10, et_logique_1_out_11, et_logique_1_out_12;

  DEMULTIPLEXEUR demultiplexeur_1 (
    .in_1(A0), .out_3(demultiplexeur_1_out_3), .in_2(Selectop), .out_4(demultiplexeur_1_out_4));
  DEMULTIPLEXEUR demultiplexeur_2 (
    .in_1(B0), .out_3(demultiplexeur_2_out_3), .in_2(Selectop), .out_4(demultiplexeur_2_out_4));
  DEMULTIPLEXEUR demultiplexeur_3 (
    .in_1(A1), .out_3(demultiplexeur_3_out_3), .in_2(Selectop), .out_4(demultiplexeur_3_out_4));
  DEMULTIPLEXEUR demultiplexeur_4 (
    .in_1(B1), .out_3(demultiplexeur_4_out_3), .in_2(Selectop), .out_4(demultiplexeur_4_out_4));
  DEMULTIPLEXEUR demultiplexeur_5 (
    .in_1(A2), .out_3(demultiplexeur_5_out_3), .in_2(Selectop), .out_4(demultiplexeur_5_out_4));
  DEMULTIPLEXEUR demultiplexeur_6 (
    .in_1(B2), .out_3(demultiplexeur_6_out_3), .in_2(Selectop), .out_4(demultiplexeur_6_out_4));
  DEMULTIPLEXEUR demultiplexeur_7 (
    .in_1(A3), .out_3(demultiplexeur_7_out_3), .in_2(Selectop), .out_4(demultiplexeur_7_out_4));
  DEMULTIPLEXEUR demultiplexeur_8 (
    .in_1(B3), .out_3(demultiplexeur_8_out_3), .in_2(Selectop), .out_4(demultiplexeur_8_out_4));
  COMPARATEUR comparateur_1 (
    .in_1(demultiplexeur_8_out_3), .in_2(demultiplexeur_6_out_3), .in_3(demultiplexeur_4_out_3),
    .in_4(demultiplexeur_2_out_3), .out_9(comparateur_1_out_9), .out_10(comparateur_1_out_10),
    .out_11(comparateur_1_out_11), .out_12(comparateur_1_out_12), .in_5(demultiplexeur_7_out_3),
    .in_6(demultiplexeur_5_out_3), .in_7(demultiplexeur_3_out_3), .in_8(demultiplexeur_1_out_3));
  ET_LOGIQUE et_logique_1 (
    .in_1(demultiplexeur_8_out_4), .in_2(demultiplexeur_6_out_4), .in_3(demultiplexeur_4_out_4),
    .in_4(demultiplexeur_2_out_4), .out_9(et_logique_1_out_9), .out_10(et_logique_1_out_10),
    .out_11(et_logique_1_out_11), .out_12(et_logique_1_out_12), .in_5(demultiplexeur_1_out_4),
    .in_6(demultiplexeur_3_out_4), .in_7(demultiplexeur_5_out_4), .in_8(demultiplexeur_7_out_4));
  MULTIPLEXEUR multiplexeur_1 (.in_2(et_logique_1_out_9), .out_4(R0), .in_1(comparateur_1_out_12), .in_3(Selectop));
  MULTIPLEXEUR multiplexeur_2 (.in_2(et_logique_1_out_10), .out_4(R1), .in_1(comparateur_1_out_11), .in_3(Selectop));
  MULTIPLEXEUR multiplexeur_3 (.in_2(et_logique_1_out_11), .out_4(R2), .in_1(comparateur_1_out_10), .in_3(Selectop));
  MULTIPLEXEUR multiplexeur_4 (.in_2(et_logique_1_out_12), .out_4(R3), .in_1(comparateur_1_out_9), .in_3(Selectop));
endmodule

module HORLOGE (
);

  wire clock_1_out, counter_2_carry, counter_3_carry;
  wire [3:0] counter_1_q, counter_2_q, counter_3_q;

  Hex_Digit_Display hex_digit_display_1 (.value(counter_1_q));  // open: dp
  Counter #(.width(4), .max('h4), .trigger("falling")) counter_1 (
    .Q(counter_1_q), .clk(counter_2_carry));  // open: load, D, count, carry, clr
  Hex_Digit_Display hex_digit_display_2 (.value(counter_2_q));  // open: dp
  Counter #(.width(4), .max('h4), .trigger("falling")) counter_2 (
    .Q(counter_2_q), .carry(counter_2_carry), .clk(counter_3_carry));  // open: load, D, count, clr
  Hex_Digit_Display hex_digit_display_3 (.value(counter_3_q));  // open: dp
  Counter #(.width(4), .max('h7)) counter_3 (
    .Q(counter_3_q), .carry(counter_3_carry), .clk(clock_1_out));  // open: load, D, count, clr
  Clock clock_1 (.out(clock_1_out));
endmodule

module ALU_1_BIT (
  input  A,
  input  B,
  input  in_3,
  input  in_4,
  input  [2:0] Selectop,
  output Result,
  output out_7
);

  wire adder_1_out, and_1_out, nand_1_out, or_1_out, xor_1_out, xor_2_out;

  xor xor_1 (xor_1_out, A, in_3);
  and and_1 (and_1_out, A, B);
  or or_1 (or_1_out, A, A);
  nand nand_1 (nand_1_out, A, A);
  xor xor_2 (xor_2_out, A, A);
  Adder #(.width(1)) adder_1 (.a(A), .b(xor_1_out), .out(adder_1_out), .cin(in_4), .cout(out_7));
  Multiplexer #(.select(3)) multiplexer_1 (
    .in0(and_1_out), .in1(or_1_out), .in2(nand_1_out), .in3(xor_2_out), .in4(adder_1_out), .out(Result),
    .sel(Selectop));  // open: in5, in6, in7, en
endmodule

module AUTRE_AUL (
  input  in_1,
  input  [2:0] in_2,
  input  [3:0] in_3,
  input  [3:0] in_4,
  input  in_5,
  input  in_6,
  input  [3:0] in_7,
  input  in_8,
  input  in_9,
  input  in_10,
  output out_11,
  output out_12,
  output out_13,
  output out_14
);

  wire alu_1_bit_1_out_7, alu_1_bit_2_out_7, alu_1_bit_3_out_7, and_1_out, and_2_out, clock_1_out,
       counter_2_carry, counter_3_carry, d_ff_1_q, d_ff_2_q, d_ff_3_q, d_ff_4_q, not_1_out, not_2_out,
       not_3_out, not_4_out, not_5_out, not_6_out, not_7_out;
  wire [3:0] counter_1_q, counter_2_q, counter_3_q;

  Hex_Digit_Display hex_digit_display_1 (.value(in_3));  // open: dp
  Hex_Digit_Display hex_digit_display_2 (.value(in_4));  // open: dp
  ALU_1_BIT alu_1_bit_1 (
    .A(in_3[0]), .B(in_4[0]), .in_3(in_1), .in_4(in_5), .Selectop(in_2), .Result(in_7[0]),
    .out_7(alu_1_bit_1_out_7));
  ALU_1_BIT alu_1_bit_2 (
    .A(in_3[1]), .B(in_4[1]), .in_3(in_1), .in_4(alu_1_bit_1_out_7), .Selectop(in_2), .Result(in_7[1]),
    .out_7(alu_1_bit_2_out_7));
  ALU_1_BIT alu_1_bit_3 (
    .A(in_3[2]), .B(in_4[2]), .in_3(in_1), .in_4(alu_1_bit_2_out_7), .Selectop(in_2), .Result(in_7[2]),
    .out_7(alu_1_bit_3_out_7));
  ALU_1_BIT alu_1_bit_4 (
    .A(in_3[3]), .B(in_4[3]), .in_3(in_1), .in_4(alu_1_bit_3_out_7), .Selectop(in_2), .Result(in_7[3]),
    .out_7(out_14));
  D_Flip_Flop d_ff_1 (.clk(clock_1_out), .D(in_7[0]), .Q(d_ff_1_q), .en(in_6));  // open: Qn, preset, reset
  D_Flip_Flop d_ff_2 (.clk(clock_1_out), .D(in_7[1]), .Q(d_ff_2_q), .en(in_8));  // open: Qn, preset, reset
  D_Flip_Flop d_ff_3 (.clk(clock_1_out), .D(in_7[2]), .Q(d_ff_3_q), .en(in_9));  // open: Qn, preset, reset
  D_Flip_Flop d_ff_4 (.clk(clock_1_out), .D(in_7[3]), .Q(d_ff_4_q), .en(in_10));  // open: Qn, preset, reset
  Hex_Digit_Display hex_digit_display_3 (.dp(d_ff_1_q));  // open: value
  Hex_Digit_Display hex_digit_display_4 (.dp(d_ff_2_q));  // open: value
  not not_1 (not_1_out, in_3[3]);
  not not_2 (not_2_out, in_4[3]);
  Hex_Digit_Display hex_digit_display_5 (.dp(d_ff_4_q));  // open: value
  not not_3 (not_3_out, in_7[3]);
  Hex_Digit_Display hex_digit_display_6 (.value(counter_1_q));  // open: dp
  Counter #(.width(4), .max('h4), .trigger("falling")) counter_1 (
    .Q(counter_1_q), .clk(counter_2_carry));  // open: load, D, count, carry, clr
  Hex_Digit_Display hex_digit_display_7 (.value(in_7));  // open: dp
  not not_4 (not_4_out, in_7[3]);
  not not_5 (not_5_out, in_7[0]);
  not not_6 (not_6_out, in_7[1]);
  not not_7 (not_7_out, in_7[2]);
  and and_1 (and_1_out, in_7[3], not_1_out, not_2_out);
  and and_2 (and_2_out, not_3_out, in_3[3], in_4[3]);
  and and_3 (out_11, not_4_out, not_5_out, not_6_out, not_7_out);
  Hex_Digit_Display hex_digit_display_8 (.dp(d_ff_3_q));  // open: value
  Hex_Digit_Display hex_digit_display_9 (.value(counter_2_q));  // open: dp
  Counter #(.width(4), .max('h4), .trigger("falling")) counter_2 (
    .Q(counter_2_q), .carry(counter_2_carry), .clk(counter_3_carry));  // open: load, D, count, clr
  or or_1 (out_13, and_1_out, and_2_out);
  Hex_Digit_Display hex_digit_display_10 (.value(counter_3_q));  // open: dp
  Counter #(.width(4), .max('h7)) counter_3 (
    .Q(counter_3_q), .carry(counter_3_carry), .clk(clock_1_out));  // open: load, D, count, clr
  Clock clock_1 (.out(clock_1_out));

  assign out_12 = in_7[3];
endmodule

// SOUS-COMP
module SOUSTRACTEUR_COMPLET (
  input  in_1,
  input  in_2,
  input  in_3,
  input  in_4,
  input  in_5,
  input  in_6,
  input  in_7,
  input  in_8,
  input  carryINstrc,
  output out_10,
  output out_11,
  output out_12,
  output out_13
);

  wire half_add_1_out_4, half_add_2_out_4, half_add_3_out_4, not_1_out, not_2_out, not_3_out, not_4_out;

  HALF_ADD half_add_1 (.in_1(carryINstrc), .in_2(in_8), .in_3(not_4_out), .out_4(half_add_1_out_4), .out_5(out_13));
  not not_1 (not_1_out, in_1);
  not not_2 (not_2_out, in_2);
  HALF_ADD half_add_2 (
    .in_1(half_add_1_out_4), .in_2(in_7), .in_3(not_3_out), .out_4(half_add_2_out_4), .out_5(out_12));
  not not_3 (not_3_out, in_3);
  not not_4 (not_4_out, in_4);
  HALF_ADD half_add_3 (
    .in_1(half_add_2_out_4), .in_2(in_6), .in_3(not_2_out), .out_4(half_add_3_out_4));  // open: out_5
  HALF_ADD half_add_4 (.in_1(half_add_3_out_4), .in_2(in_5), .in_3(not_1_out), .out_4(out_10), .out_5(out_11));
endmodule

// UR
module UNITE_ARITHMETIQUE (
  input  Selectop,
  input  B3,
  input  B2,
  input  B1,
  input  B0,
  input  A0,
  input  CARRYinAD,
  input  A1,
  input  A2,
  input  A3,
  input  CARRYinST,
  output R0,
  output R1,
  output R2,
  output R3
);

  wire demultiplexeur_1_out_3, demultiplexeur_1_out_4, demultiplexeur_2_out_3, demultiplexeur_2_out_4,
       demultiplexeur_3_out_3, demultiplexeur_3_out_4, demultiplexeur_4_out_3, demultiplexeur_4_out_4,
       demultiplexeur_5_out_3, demultiplexeur_5_out_4, demultiplexeur_6_out_3, demultiplexeur_6_out_4,
       demultiplexeur_7_out_3, demultiplexeur_7_out_4, demultiplexeur_8_out_3, demultiplexeur_8_out_4,
       full_add_1_out_10, full_add_1_out_11, full_add_1_out_12, full_add_1_out_13,
       soustracteur_complet_1_out_10, soustracteur_complet_1_out_11, soustracteur_complet_1_out_12,
       soustracteur_complet_1_out_13;

  DEMULTIPLEXEUR demultiplexeur_1 (
    .in_1(A0), .out_3(demultiplexeur_1_out_3), .in_2(Selectop), .out_4(demultiplexeur_1_out_4));
  DEMULTIPLEXEUR demultiplexeur_2 (
    .in_1(B0), .out_3(demultiplexeur_2_out_3), .in_2(Selectop), .out_4(demultiplexeur_2_out_4));
  DEMULTIPLEXEUR demultiplexeur_3 (
    .in_1(A1), .out_3(demultiplexeur_3_out_3), .in_2(Selectop), .out_4(demultiplexeur_3_out_4));
  DEMULTIPLEXEUR demultiplexeur_4 (
    .in_1(B1), .out_3(demultiplexeur_4_out_3), .in_2(Selectop), .out_4(demultiplexeur_4_out_4));
  DEMULTIPLEXEUR demultiplexeur_5 (
    .in_1(A2), .out_3(demultiplexeur_5_out_3), .in_2(Selectop), .out_4(demultiplexeur_5_out_4));
  DEMULTIPLEXEUR demultiplexeur_6 (
    .in_1(B2), .out_3(demultiplexeur_6_out_3), .in_2(Selectop), .out_4(demultiplexeur_6_out_4));
  DEMULTIPLEXEUR demultiplexeur_7 (
    .in_1(A3), .out_3(demultiplexeur_7_out_3), .in_2(Selectop), .out_4(demultiplexeur_7_out_4));
  DEMULTIPLEXEUR demultiplexeur_8 (
    .in_1(B3), .out_3(demultiplexeur_8_out_3), .in_2(Selectop), .out_4(demultiplexeur_8_out_4));
  FULL_ADD full_add_1 (
    .in_9(CARRYinAD), .in_5(demultiplexeur_7_out_3), .in_6(demultiplexeur_5_out_3),
    .in_7(demultiplexeur_3_out_3), .in_8(demultiplexeur_1_out_3), .in_1(demultiplexeur_8_out_3),
    .in_2(demultiplexeur_6_out_3), .in_3(demultiplexeur_4_out_3), .in_4(demultiplexeur_2_out_3),
    .out_10(full_add_1_out_10), .out_11(full_add_1_out_11), .out_12(full_add_1_out_12),
    .out_13(full_add_1_out_13));
  SOUSTRACTEUR_COMPLET soustracteur_complet_1 (
    .carryINstrc(CARRYinST), .in_5(demultiplexeur_7_out_4), .in_6(demultiplexeur_5_out_4),
    .in_7(demultiplexeur_3_out_4), .in_8(demultiplexeur_1_out_4), .in_1(demultiplexeur_8_out_4),
    .in_2(demultiplexeur_6_out_4), .in_3(demultiplexeur_4_out_4), .in_4(demultiplexeur_2_out_4),
    .out_10(soustracteur_complet_1_out_10), .out_11(soustracteur_complet_1_out_11),
    .out_12(soustracteur_complet_1_out_12), .out_13(soustracteur_complet_1_out_13));
  MULTIPLEXEUR multiplexeur_1 (
    .in_2(soustracteur_complet_1_out_13), .out_4(R0), .in_1(full_add_1_out_13), .in_3(Selectop));
  MULTIPLEXEUR multiplexeur_2 (
    .in_2(soustracteur_complet_1_out_12), .out_4(R1), .in_1(full_add_1_out_12), .in_3(Selectop));
  MULTIPLEXEUR multiplexeur_3 (
    .in_2(soustracteur_complet_1_out_11), .out_4(R2), .in_1(full_add_1_out_11), .in_3(Selectop));
  MULTIPLEXEUR multiplexeur_4 (
    .in_2(soustracteur_complet_1_out_10), .out_4(R3), .in_1(full_add_1_out_10), .in_3(Selectop));
endmodule

module UNITE_CHARGEMENT (
  input  B3,
  input  B2,
  input  B1,
  input  B0,
  input  A3,
  input  A2,
  input  A1,
  input  A0,
  input  SelectOperat,
  input  CARRYinSTR,
  input  CARRYinADD,
  input  B3_2,
  input  B2_2,
  input  B1_2,
  input  B0_2,
  input  A3_2,
  input  A2_2,
  input  A1_2,
  input  A0_2,
  input  Enable,
  input  SelectUnite,
  input  SelectOperat_2,
  output [3:0] RESULTAT
);

  wire CLOCK_out, counter_1_carry, counter_2_carry, counter_3_carry;
  wire [3:0] counter_1_q, counter_2_q, counter_3_q, multiplexer_1_out, unite_arithmetique_1_r0,
       unite_logique_1_r0;

  UNITE_ARITHMETIQUE unite_arithmetique_1 (
    .A0(A0), .A1(A1), .A2(A2), .A3(A3), .R0(unite_arithmetique_1_r0[0]), .R1(unite_arithmetique_1_r0[1]),
    .R2(unite_arithmetique_1_r0[2]), .R3(unite_arithmetique_1_r0[3]), .B3(B3), .B2(B2), .B1(B1), .B0(B0),
    .Selectop(SelectOperat), .CARRYinST(CARRYinSTR), .CARRYinAD(CARRYinADD));
  UNITE_LOGIQUE unite_logique_1 (
    .A0(A0_2), .A1(A1_2), .A2(A2_2), .A3(A3_2), .R0(unite_logique_1_r0[0]), .R1(unite_logique_1_r0[1]),
    .R2(unite_logique_1_r0[2]), .R3(unite_logique_1_r0[3]), .B3(B3_2), .B2(B2_2), .B1(B1_2), .B0(B0_2),
    .Selectop(SelectOperat_2));
  Multiplexer #(.width(4)) multiplexer_1 (
    .in0(unite_arithmetique_1_r0), .in1(unite_logique_1_r0), .out(multiplexer_1_out), .sel(SelectUnite));  // open: en
  Register #(.width(4)) register_1 (
    .D(multiplexer_1_out), .en(Enable), .Q(RESULTAT), .clk(counter_1_carry));  // open: clr
  Hex_Digit_Display hex_digit_display_1 (.value(counter_1_q));  // open: dp
  Counter #(.width(4), .max('h4), .trigger("falling")) counter_1 (
    .Q(counter_1_q), .carry(counter_1_carry), .clk(counter_2_carry));  // open: load, D, count, clr
  Hex_Digit_Display hex_digit_display_2 (.value(RESULTAT));  // open: dp
  Hex_Digit_Display hex_digit_display_3 (.value(counter_2_q));  // open: dp
  Counter #(.width(4), .max('h4), .trigger("falling")) counter_2 (
    .Q(counter_2_q), .carry(counter_2_carry), .clk(counter_3_carry));  // open: load, D, count, clr
  Hex_Digit_Display hex_digit_display_4 (.value(counter_3_q));  // open: dp
  Counter #(.width(4), .max('h7)) counter_3 (
    .Q(counter_3_q), .carry(counter_3_carry), .clk(CLOCK_out));  // open: load, D, count, clr
  Clock CLOCK (.out(CLOCK_out));

  // Notes on the sheet:
  //   UR{SelectOperat[Soustrac=1;Adder=0]}
  //   CARRYinSTR=1; CARRYinADD=1
  //   UL{SelectOperat[Et-Log=1; Comp=0]}
  //   Enable=1
  //   SelectUnite{UR=0; UL=1}
endmodule
